# Fritzing sketch Chem (saved by Fritzing 0.9.3b)

parts:
  Часть1 = Arduino Uno (Rev3) - ICSP
  S1 = H-Bridge with L298N
  M1 = DC Motor
  BAT1 = Battery Holders [package=lipo-1100mAh]
  BAT2 = Battery Holders [package=lipo-1100mAh]
  M2 = DC Motor
  M3 = DC Motor
  M4 = DC Motor
  Часть5 = Ambient Light Sensor (TEMT6000 Breakout Board)
  Часть6 = Ambient Light Sensor (TEMT6000 Breakout Board)
  Часть7 = Ambient Light Sensor (TEMT6000 Breakout Board)

nets:
  N1: Часть1.A0, Часть5.S
  N2: Часть1.A1, Часть7.S
  N3: Часть1.A2, Часть6.S
  N4: Часть1.D8, S1.IN4
  N5: Часть1.D9_PWM, S1.ENB
  N6: Часть1.D3_PWM, S1.ENA
  N7: Часть1.D5_PWM, S1.IN1
  N8: Часть1.D6_PWM, S1.IN2
  N9: Часть1.D7, S1.IN3
  VCC: Часть1.5V, S1.5V, Часть5.VCC, Часть6.VCC, Часть7.VCC
  GND: Часть1.GND, S1.GND, BAT1.-, Часть5.GND, Часть6.GND, Часть7.GND
  N10: Часть1.VIN, BAT2.+
  N11: S1.M1-01, M1.pin_2, M2.pin_2
  N12: S1.M1-02, M1.pin_1, M2.pin_1
  N13: S1.M2-01, M3.pin_2, M4.pin_2
  N14: S1.M2-02, M3.pin_1, M4.pin_1
  N15: BAT1.+, BAT2.-

custom parts:
  H-Bridge with L298N: h-bridge
