# Fritzing sketch HandBot (saved by Fritzing 0.9.3b)

parts:
  J1 = Basic Servo [part_number="Servo 3"]
  Часть1 = 16-Channel 12-bit PWM Servo Driver - I2C [part_number=815]
  Часть2 = Arduino Nano (Rev3.0)
  J2 = Basic Servo [part_number="Servo 2"]
  J3 = Basic Servo [part_number="Servo 1"]
  VCC1 = 4 x AAA Battery Mount
  S1 = SPST Switch [package=switch-spdt_kit]
  Часть3 = Thumb Joystick
  Часть4 = Thumb Joystick
  Часть5 = Thumb Joystick
  Часть6 = Thumb Joystick
  Часть7 = Thumb Joystick

nets:
  GND: J1.gnd, Часть1.GND, Часть2.GND, J2.gnd, J3.gnd, S1.O, Часть3.GND
  VCC: J1.vcc, Часть1.5.0V, J2.vcc, J3.vcc
  N1: J1.pulse, Часть1.PWM10
  VCC_2: Часть1.VCC, VCC1.+, Часть3.VCC
  N2: Часть1.SDA, Часть2.A4
  N3: Часть1.SCL, Часть2.A5
  N4: Часть1.PWM9, J2.pulse
  N5: Часть1.PWM8, J3.pulse
  N6: Часть2.A7, Часть3.VERT
  N7: Часть2.A3, Часть4.VERT
  N8: Часть2.A2, Часть5.VERT
  N9: Часть2.A1, Часть7.VERT
  N10: Часть2.A0, Часть6.VERT
  N11: VCC1.-, S1.P

custom parts:
  16-Channel 12-bit PWM Servo Driver - I2C: You want to make a cool robot, maybe a hexapod walker, or maybe just a piece of art with a lot of moving parts. Or maybe you want to drive a lot of LEDs with precise PWM output. Using only two pins, control 16 free-running PWM outputs! You can even chain up 62 breakouts to control up to 992 PWM outputs.
