# Fritzing sketch fr_pS (saved by Fritzing 0.9.3b)

parts:
  Часть1 = Arduino Nano (Rev3.0)
  Часть2 = LED Matrix - Serial Interface - Red/Green/Blue
  T1 = LM35 Temperature Sensor [package="TO92 [THT]"]  # not connected
  M1 = DC Motor  # not connected
  hc-sr1 = hc-sr04
  LED1 = LED - 3mm [color="Red (633nm)" package="3 mm [THT]"]  # not connected
  LED2 = LED - 3mm [color="Red (633nm)" package="3 mm [THT]"]  # not connected
  LED3 = LED - 3mm [color="Red (633nm)" package="3 mm [THT]"]  # not connected
  LED4 = LED - 3mm [color="Red (633nm)" package="3 mm [THT]"]  # not connected
  LED5 = LED - 3mm [color="Red (633nm)" package="3 mm [THT]"]  # not connected
  D1 = Zener Diode [part_number=1N4732A breakdown_voltage=3.6V package="300 mil [THT]"]
  Часть4 = DeuLigne 1.1 - The Snootlab's LCD shield for Arduino
  J1 = Piezo Speaker  # not connected
  S1 = Pushbutton [package="[THT]"]
  U3 = POT [package=3362u]
  LED6 = RGB LED - (4 legs) [package="5 mm [THT]"]  # not connected
  S2 = Pushbutton [package="[THT]"]
  S3 = Pushbutton [package="[THT]"]
  R1 = Resistor [tolerance=±5% resistance=10k package=THT]
  R2 = Resistor [tolerance=±5% resistance=10k package=THT]
  R3 = Resistor [tolerance=±5% resistance=10k package=THT]
  R4 = Resistor [tolerance=±5% resistance=100 package=THT]  # not connected
  R5 = Resistor [tolerance=±5% resistance=100 package=THT]  # not connected
  R6 = Resistor [tolerance=±5% resistance=100 package=THT]  # not connected
  R7 = Resistor [tolerance=±5% resistance=100 package=THT]  # not connected
  R8 = Resistor [tolerance=±5% resistance=100 package=THT]  # not connected

nets:
  N1: Часть1.D3, D1.cathode
  N2: Часть1.D5, Часть2.MOSI
  N3: Часть1.D6, Часть2.CS
  N4: Часть1.D7, Часть2.SCK
  N5: Часть1.A7, U3.S
  N6: Часть1.A5, Часть4.A5(CLK)
  N7: Часть1.A4, Часть4.A4(SDA)
  N8: Часть1.A3, S1.Pin_1, S1.Pin_2
  N9: Часть1.A2, S2.Pin_1, S2.Pin_2
  N10: Часть1.A1, hc-sr1.Trig
  N11: Часть1.A0, hc-sr1.Echo
  N12: Часть1.D13/SCK, S3.Pin_1, S3.Pin_2
  N13: S1.Pin_3, S1.Pin_4, R3.Pin_1
  N14: S2.Pin_3, S2.Pin_4, R2.Pin_1
  N15: S3.Pin_4, R1.Pin_1

notes:
  D9
  D10
  D11
  D8
  D12
  RGB-LED
  Piezo-speacker
  LM35
  Led-matrix 8x8
