# Fritzing sketch Chem (saved by Fritzing 0.9.3b)

parts:
  Часть1 = Arduino Nano (Rev3.0)
  J1 = Basic Servo
  BAT1 = Battery Holders [package=lipo-1100mAh]
  BAT2 = Battery Holders [package=lipo-1100mAh]
  hc-sr1 = hc-sr04

nets:
  GND: Часть1.GND, J1.gnd, BAT1.-, hc-sr1.GND
  N1: Часть1.D4, hc-sr1.Trig
  N2: Часть1.D6, hc-sr1.Echo
  N3: Часть1.VIN, BAT2.+
  VCC: Часть1.5V, J1.vcc, hc-sr1.VCC
  N4: BAT1.+, BAT2.-
