# Fritzing sketch chem (saved by Fritzing 0.9.3b)
breadboards: 1

parts:
  M1 = DC Motor  # not connected
  Часть1 = Arduino Nano (Rev3.0)
  M2 = fc-51 [package=THT]
  VCC1 = Battery block 9V
  IC1 = L293D [package=THT]

nets:
  N1: Часть1.GND, M2.pin2, VCC1.-, IC1.In_1, IC1.0V
  N2: Часть1.D2, M2.pin1
  N3: Часть1.D11/MOSI, IC1.In_2
  N4: Часть1.5V, M2.pin3
