# Fritzing sketch greenHouse (saved by Fritzing 0.9.3b)

parts:
  Grove1 = Grove Light Sensor  # not connected
  Часть1 = Soil Moisture Sensor  # not connected
  Часть2 = Arduino Nano (Rev3.0)  # not connected
  LED1 = LEDs [package=led10mm]
  Part3 = Lilypad Battery Connect
  Mod1 = generic-ac-power-supply [package=THT]  # not connected
  JP1 = LITTLEBITS_FEMALE [package=little_bits_female]  # not connected
  JP2 = Header 2 [package=molex-1x2_lock]  # not connected
  KY-1 = Keyes Relay [package=THT]  # not connected
  J1 = HANRUN RJ-45 [package=hanrun]  # not connected

nets:
  N1: LED1.A, Part3.+

notes:
  240V AC power supply

custom parts:
  LEDs: LEDs Standard schematic elements and footprints for 5mm, 3mm, 1206, and 0603 sized LEDs. 5mm - Spark Fun Electronics SKU : COM-00529 (and others)
  generic-ac-power-supply: Generic ac power supply module. Use as is, or customize the svgs to fit your particular device (as they are all different.) Provides AC input and single DC output. PCB is generic and will need modifications if you intend to do a pcb mount.
  Keyes Relay: The Keyes 5V relay module is suitable for SCM development, home appliance control. It uses a 5V~12V TIL control signal which can control DC / AC signal.
  HANRUN RJ-45: RJ-45 with LEDs HANRUN HR911105A
